# Fritzing sketch atmega (saved by Fritzing 0.9.3b)
breadboards: 1

parts:
  U1 = atmega328 [package=dip]
  BO1 = BO320XS [chip_label=BO230XS package="DIP (Dual Inline) [THT]"]
  XTAL1 = Crystal [frequency="16 Mhz" package=THT]
  R1 = Resistor [tolerance=±5% resistance=1k package=THT]
  RESET = Pushbutton [package=THT]
  C1 = Ceramic Capacitor [capacitance=100nF package="100 mil [THT, multilayer]"]
  C2 = Ceramic Capacitor [capacitance=100nF package="100 mil [THT, multilayer]"]
  C3 = Ceramic Capacitor [capacitance=100nF package="100 mil [THT, multilayer]"]

nets:
  N1: U1.RESET, BO1.CTS, R1.Pin_1, RESET.leg1
  N2: U1.D0_(RX), U1.D11_(PWM), BO1.TXD
  N3: U1.D1_(TX), U1.D12, BO1.RXD
  5V: U1.VCC, U1.AVCC, U1.AREF, BO1.VCC, R1.Pin_0, C1.0, C2.0, C3.0
  GND: U1.GND, BO1.GND, RESET.leg0, C1.1, C2.1
  N4: U1.XLAT1, XTAL1.pin_0, C3.1
  N5: U1.XLAT2, XTAL1.pin_1
  N6: U1.D13, BO1.RTS

custom parts:
  BO320XS: USB bootloader
